// Logisim project 4-bit-cpu-v2.circ as structural Verilog: 2 circuits, main circuit main
module main (
  input  in_1,
  input  in_2,
  input  in_3,
  input  in_4,
  input  RESET
);

  wire BREAK, clock_1_out, counter_2_carry, decoder_1_out0, decoder_1_out1, decoder_1_out2, decoder_1_out3,
       decoder_2_out0, decoder_2_out1, decoder_2_out2, decoder_2_out3, LDPC, nop_1_p6, nop_1_p7, nop_1_p8,
       nop_1_p9, nop_1_p10, nop_1_p11, nop_1_p12, not_1_out, not_2_out, or_1_out, RAE, RWRAM, ZE;
  wire [1:0] BUS_MUX, counter_2_q;
  wire [3:0] counter_1_q, multiplexer_1_out, ram_1_data, register_1_q, register_2_q, register_3_q, rom_1_data;

  // Probe on LDPC
  not not_1 (not_1_out, LDPC);
  Clock clock_1 (.out(clock_1_out));
  Counter #(.width(4), .max('hf)) counter_1 (
    .load(LDPC), .D(multiplexer_1_out), .count(not_1_out), .Q(counter_1_q), .clk(clock_1_out), .clr(RESET));  // open: carry
  Register #(.width(4)) register_1 (.D(multiplexer_1_out), .en(RAE), .Q(register_1_q), .clk(clock_1_out));  // open: clr
  // Probe on RAE
  RAM #(.addrWidth(4), .dataWidth(4)) ram_1 (
    .addr(register_1_q), .data(ram_1_data), .clk(clock_1_out), .ld(not_2_out));  // open: sel, clr
  not not_2 (not_2_out, RWRAM);
  ROM #(.addrWidth(4), .dataWidth(4)) rom_1 (.addr(counter_1_q), .data(rom_1_data));  // open: sel
  assign ram_1_data = RWRAM ? multiplexer_1_out : 4'bz;  // Controlled_Buffer controlled_buffer_1
  // Probe on RWRAM
  Register #(.width(4)) register_2 (.D(multiplexer_1_out), .en(ZE), .Q(register_2_q), .clk(clock_1_out));  // open: clr
  // Probe on ZE
  Register #(.width(4)) register_3 (.D(rom_1_data), .en(or_1_out), .Q(register_3_q), .clk(clock_1_out));  // open: clr
  Multiplexer #(.select(2), .width(4)) multiplexer_1 (
    .in0(rom_1_data), .in1(ram_1_data), .in2(register_2_q), .out(multiplexer_1_out), .sel(BUS_MUX), .en(1'b1));  // open: in3
  Decoder #(.select(4)) decoder_1 (
    .out0(decoder_1_out0), .out1(decoder_1_out1), .out2(decoder_1_out2), .out3(decoder_1_out3),
    .sel(register_3_q));  // open: out4, out5, out6, out7, out8, out9, out10, out11, out12, out13, out14, out15, en
  or or_1 (or_1_out, BREAK, decoder_1_out0, counter_2_carry);
  Counter #(.width(2), .max('h3)) counter_2 (
    .Q(counter_2_q), .carry(counter_2_carry), .clk(clock_1_out), .clr(or_1_out));  // open: load, D, count
  Decoder #(.select(2)) decoder_2 (
    .out0(decoder_2_out0), .out1(decoder_2_out1), .out2(decoder_2_out2), .out3(decoder_2_out3),
    .sel(counter_2_q));  // open: en
  // NOP nop_1: pin names not known; wires that end beside it: decoder_2_out0, decoder_2_out1, decoder_2_out2, decoder_2_out3, decoder_1_out0, nop_1_p6, nop_1_p7, nop_1_p8, nop_1_p9, nop_1_p10, nop_1_p11, nop_1_p12
  buf or_2 (LDPC, nop_1_p6);  // OR_Gate
  buf or_3 (ZE, nop_1_p7);  // OR_Gate
  buf or_4 (RWRAM, nop_1_p8);  // OR_Gate
  buf or_5 (RAE, nop_1_p9);  // OR_Gate
  buf or_6 (BUS_MUX[0], nop_1_p10);  // OR_Gate
  buf or_7 (BUS_MUX[1], nop_1_p11);  // OR_Gate
  buf or_8 (BREAK, nop_1_p12);  // OR_Gate

  // Notes on the sheet:
  //   LDPC
  //   RAM
  //   PROG MEM
  //   contents of rom_1 (hex, n*v repeats v):
  //   1 2 3 4 5 6 7 1 9 a b c d e f
  //   R/W RAM
  //   Z REG
  //   INSTRUCTION REG
  //   hacer el break
endmodule

module NOP (
  input  CS0,
  input  CS1,
  input  CS2,
  input  CS3,
  input  ENABLE,
  output LDPCO,
  output ZE,
  output RWRAM,
  output RAEO,
  output BMX0,
  output BMX1,
  output BRK
);


  assign BMX0 = 1'b0;
  assign BMX1 = 1'b0;
  assign BRK = 1'b0;
  assign CS1 = CS0;
  assign CS2 = CS0;
  assign CS3 = CS0;
  assign ENABLE = CS0;
  assign LDPCO = 1'b0;
  assign RAEO = 1'b0;
  assign RWRAM = 1'b0;
  assign ZE = 1'b0;
  // also tied to GND on the sheet: CS0
endmodule
